# Fritzing sketch jetson_finder_schmetics_last_project (saved by Fritzing 0.9.4)
breadboards: 2

parts:
  Jetson_Nano2 = Jetson Nano
  LED2 = LED - 5mm [color="Red (633nm)" package="5 mm [THT]"]
  R2 = Resistor [tolerance=±5% resistance=220 package=THT]
  HC-SR04_Sensor_1 = HC-SR04 Ultrasonic Distance Sensor
  LED3 = RGB LED (com. cathode, rbg) [package="5 mm [THT]"]
  SG1 = Buzzer 12mm [package=buzzer-ccv]
  S1 = Momentary Switch [package=tactile-pth]
  M1 = Dagu DGServo 9g (Pan and tilt) [part_number=RS001B]
  LCD1 = LCD screen
  R3 = Rotary Potentiometer (Small) [maximum_resistance=100kΩ package=THT]
  R4 = Resistor [tolerance=±5% resistance=220 package=THT]
  R5 = Rotary Potentiometer (Small) [maximum_resistance=100kΩ package=THT]  # not connected

nets:
  N1: Jetson_Nano2.GND, S1.1, LCD1.RS, LCD1.DB7
  N2: Jetson_Nano2.GPIO22, HC-SR04_Sensor_1.ECHO
  N3: Jetson_Nano2.3V3, HC-SR04_Sensor_1.TRIG
  GND: Jetson_Nano2.GPIO19, R2.Pin_0, HC-SR04_Sensor_1.GND, LED3.red_anode, SG1.1, M1.gnd, LCD1.VSS, LCD1.R/W, LCD1.LED-, R3.leg2
  VCC: Jetson_Nano2.GPIO26, HC-SR04_Sensor_1.VCC, M1.vcc, LCD1.VDD, R3.leg1, R4.Pin_1
  N4: Jetson_Nano2.ID_SC, LCD1.E
  N5: Jetson_Nano2.GPIO18, LCD1.DB4
  N6: Jetson_Nano2.GPIO15, LCD1.DB5
  N7: Jetson_Nano2.GPIO14, LCD1.DB6
  N8: LED2.cathode, SG1.2
  N9: LED2.anode, S1.3
  N10: R2.Pin_1, LED3.common_cathode
  N11: LED3.blue_anode, LCD1.V0, R3.wiper
  N12: LED3.green_anode, S1.2, M1.pulse
  N13: LCD1.LED+, R4.Pin_0
